// Logisim project assignment3.circ as structural Verilog
module main (
  input  [2:0] in_1
);

  wire [7:0] assignment3_1_display;

  assignment3 assignment3_1 (.sel(in_1), .display(assignment3_1_display));
  _7_Segment_Display u_7_segment_display_1 (
    .g(assignment3_1_display[0]), .f(assignment3_1_display[1]), .a(assignment3_1_display[2]),
    .b(assignment3_1_display[3]), .e(assignment3_1_display[4]), .d(assignment3_1_display[5]),
    .c(assignment3_1_display[6]), .dp(assignment3_1_display[7]));
endmodule

// VHDL entity assignment3, as the project stores it:
library ieee;
use ieee.std_logic_1164.all;

entity assignment3 is
    port(
        sel     : in  std_logic_vector(2 downto 0);
        display : out std_logic_vector(7 downto 0)
    );
end entity assignment3;

architecture bhv of assignment3 is
begin
    process(sel)
    begin
        case sel is
            --  비트 위치:  7  6  5  4  3  2  1  0
            --  담당 세그: dp  C  D  E  B  A  F  G
            when "000" => display <= "01011111"; -- 'a' (1, 2, 3, 4, 6, 0)
            when "001" => display <= "01110011"; -- 'b' (1, 4, 5, 6, 0)
            when "010" => display <= "00110110"; -- 'c' (1, 2, 4, 5)
            when "011" => display <= "01111001"; -- 'd' (3, 4, 5, 6, 0)
            when "100" => display <= "00010111"; -- 'f' (1, 2, 4, 0)
            when "101" => display <= "01101111"; -- 'g' (1, 2, 3, 5, 6, 0)
            when others => display <= "00000000";
        end case;
    end process;
end architecture bhv;
