// Logisim project assignment4.circ as structural Verilog
module main (
  output out_1
);

  wire [24:0] dipswitch_1_p1;

  // DipSwitch #(.number(12)) dipswitch_1: pin names not known; wires that end beside it: dipswitch_1_p1[0], dipswitch_1_p1[1], dipswitch_1_p1[2], dipswitch_1_p1[3], dipswitch_1_p1[4], dipswitch_1_p1[5]
  // DipSwitch #(.number(13)) dipswitch_2: pin names not known; wires that end beside it: dipswitch_1_p1[6], dipswitch_1_p1[7], dipswitch_1_p1[8], dipswitch_1_p1[9], dipswitch_1_p1[10], dipswitch_1_p1[11], dipswitch_1_p1[12], dipswitch_1_p1[13], dipswitch_1_p1[14], dipswitch_1_p1[15], dipswitch_1_p1[16], dipswitch_1_p1[17], dipswitch_1_p1[18], dipswitch_1_p1[19], dipswitch_1_p1[20], dipswitch_1_p1[21], dipswitch_1_p1[22], dipswitch_1_p1[23], dipswitch_1_p1[24]
  vote25 vote25_1 (.vt(dipswitch_1_p1), .result(out_1));
endmodule

// VHDL entity vote25, as the project stores it:
library ieee;
use ieee.std_logic_1164.all;
use ieee.std_logic_arith.all;
use ieee.std_logic_unsigned.all;

entity vote25 is
    port(
        vt     : in  std_logic_vector(25 downto 1); 
        result : out std_logic                      
    );
end entity vote25;

architecture bhv of vote25 is
begin
    process(vt)
        variable sum: integer range 0 to 25;
    begin
        sum := 0;
        
        
        for i in 1 to 25 loop
            if (vt(i) = '1') then
                sum := sum + 1;
            end if;
        end loop;

       
        if sum >= 13 then
            result <= '1';
        else
            result <= '0';
        end if;
    end process;
end architecture bhv;
