// Logisim project assignment5.circ as structural Verilog
module main (
  input  in_1
);

  wire [7:0] assignment5_1_display;
  wire [12:0] dipswitch_1_p1;

  // DipSwitch #(.number(13)) dipswitch_1: pin names not known; wires that end beside it: dipswitch_1_p1[0], dipswitch_1_p1[1], dipswitch_1_p1[2], dipswitch_1_p1[3], dipswitch_1_p1[4], dipswitch_1_p1[5], dipswitch_1_p1[6], dipswitch_1_p1[7], dipswitch_1_p1[8], dipswitch_1_p1[9], dipswitch_1_p1[10], dipswitch_1_p1[11], dipswitch_1_p1[12]
  assignment5 assignment5_1 (.en(in_1), .vt(dipswitch_1_p1), .display(assignment5_1_display));
  _7_Segment_Display u_7_segment_display_1 (
    .g(assignment5_1_display[0]), .f(assignment5_1_display[1]), .a(assignment5_1_display[2]),
    .b(assignment5_1_display[3]), .e(assignment5_1_display[4]), .d(assignment5_1_display[5]),
    .c(assignment5_1_display[6]), .dp(assignment5_1_display[7]));
endmodule

// VHDL entity assignment5, as the project stores it:
library ieee;
use ieee.std_logic_1164.all;
use ieee.std_logic_arith.all;
use ieee.std_logic_unsigned.all;

entity assignment5 is
    port(
        en      : in  std_logic;
        vt      : in  std_logic_vector(13 downto 1);
        display : out std_logic_vector(7 downto 0)
    );
end entity assignment5;

architecture bhv of assignment5 is
begin
    process(en, vt)
        variable sum : integer range 0 to 15;
    begin
        if en = '0' then
            -- 강의 예제(이미지 4) 방식: en이 '0'일 때 High-Impedance(Hi-Z) 상태로 출력 개방
            display <= "ZZZZZZZZ"; 
        else
            -- 13개 입력 중 '1'의 개수 집계
            sum := 0;
            for i in 1 to 13 loop
                if (vt(i) = '1') then
                    sum := sum + 1;
                end if;
            end loop;

            -- 득표 수(sum)에 따라 16진수(0~D) 7-세그먼트 비트 패턴 출력
            case sum is
                when 0  => display <= "01111110"; -- '0'
                when 1  => display <= "01001000"; -- '1'
                when 2  => display <= "00111101"; -- '2'
                when 3  => display <= "01101101"; -- '3'
                when 4  => display <= "01001011"; -- '4'
                when 5  => display <= "01100111"; -- '5'
                when 6  => display <= "01110111"; -- '6'
                when 7  => display <= "01001110"; -- '7'
                when 8  => display <= "01111111"; -- '8'
                when 9  => display <= "01101111"; -- '9'
                when 10 => display <= "01011111"; -- 'A'
                when 11 => display <= "01110011"; -- 'b'
                when 12 => display <= "00110110"; -- 'C'
                when 13 => display <= "01111001"; -- 'd'
                when 14 => display <= "00110111"; -- 'E'
                when 15 => display <= "00010111"; -- 'F'
                when others => display <= "00000000";
            end case;
        end if;
    end process;
end architecture bhv;
