// Logisim project not_gate.circ as structural Verilog
module main (
  input  in_1,
  input  in_2,
  output out_3,
  output out_4
);

  not not_1 (out_4, in_2);
  not_gate not_gate_1 (.a(in_1), .y(out_3));
endmodule

// VHDL entity not_gate, as the project stores it:
library IEEE;
use IEEE.STD_LOGIC_1164.ALL;

entity not_gate is
    Port ( a : in  STD_LOGIC;
           y : out STD_LOGIC);
end not_gate;

architecture Behavioral of not_gate is
begin
    y <= not a;
end Behavioral;
